# Fritzing sketch SequencialSwitch (saved by Fritzing 0.9.3b)
stripboards: 1

parts:
  J8 = female pin header, 1 pin [form="♀ (female)" part_number="gnd point"]
  C2 = Electrolytic Capacitor [capacitance=47µF voltage=35V package="100 mil [THT, electrolytic]"]
  C1 = Electrolytic Capacitor [capacitance=47µF voltage=35V package="100 mil [THT, electrolytic]"]
  SW1 = Toggle Switch [part_number="3 position switch" package=THT]
  D1 = Diode [part_number=1N5819WS package=sod-323]
  D2 = Diode [part_number=1N5819WS package=sod-323]
  D8 = Diode [part_number=1N4148 package=sod523]
  D7 = Diode [part_number=1N4148 package=sod523]
  D6 = Diode [part_number=1N4148 package=sod523]
  D5 = Diode [part_number=1N4148 package=sod523]
  C3 = Ceramic Capacitor [capacitance=10nF voltage=35V package="0603 [SMD, multilayer]"]
  C4 = Ceramic Capacitor [capacitance=10nF voltage=35V package="0603 [SMD, multilayer]"]
  C5 = Ceramic Capacitor [capacitance=100nF voltage=35V package="0603 [SMD, multilayer]"]
  C6 = Ceramic Capacitor [capacitance=100nF voltage=35V package="0603 [SMD, multilayer]"]
  C7 = Ceramic Capacitor [capacitance=10nF voltage=35V package="0603 [SMD, multilayer]"]
  R11 = Resistor [tolerance=±1% resistance=1k package="0603 [SMD]"]
  R15 = Resistor [tolerance=±1% resistance=1k package="0603 [SMD]"]
  R14 = Resistor [tolerance=±1% resistance=1k package="0603 [SMD]"]
  R18 = Resistor [tolerance=±1% resistance=1k package="0603 [SMD]"]
  R19 = Resistor [tolerance=±1% resistance=1k package="0603 [SMD]"]
  J9 = double row smd female pin header, 10 pins [form="♀ (female)"]
  IC2 = SSOP16 [chip_label=DG412 package=SSOP]
  R9 = Resistor [tolerance=±1% resistance=1k package="0402 [SMD]"]
  R20 = Resistor [tolerance=±1% resistance=1k package="0402 [SMD]"]
  IC3 = SSOP16 [chip_label=DG412 package=SSOP]
  R10 = Resistor [tolerance=±1% resistance=1k package="0402 [SMD]"]
  R12 = Resistor [tolerance=±1% resistance=1k package="0402 [SMD]"]
  R12_2 = Resistor [tolerance=±1% resistance=1k package="0402 [SMD]"]
  R13 = Resistor [tolerance=±1% resistance=1k package="0402 [SMD]"]
  R16 = Resistor [tolerance=±1% resistance=1k package="0402 [SMD]"]
  R17 = Resistor [tolerance=±1% resistance=1k package="0402 [SMD]"]
  IC1 = SSOP16 [chip_label=4017 package=SSOP]
  R1 = Resistor [tolerance=±1% resistance=47k package="0402 [SMD]"]
  Q2 = NPN-Transistor [package="SOT-23 [SMD]"]
  Q1 = NPN-Transistor [package="SOT-23 [SMD]"]
  R2 = Resistor [tolerance=±1% resistance=10k package="0402 [SMD]"]
  R3 = Resistor [tolerance=±1% resistance=10k package="0402 [SMD]"]
  D3 = Diode [package=sod523]
  R4 = Resistor [tolerance=±1% resistance=47k package="0402 [SMD]"]
  Q4 = NPN-Transistor [package="SOT-23 [SMD]"]
  R5 = Resistor [tolerance=±1% resistance=10k package="0402 [SMD]"]
  R7 = Resistor [tolerance=±1% resistance=10k package="0402 [SMD]"]
  Q3 = NPN-Transistor [package="SOT-23 [SMD]"]
  R8 = Resistor [tolerance=±1% resistance=47k package="0402 [SMD]"]
  D4 = Diode [package=sod523]
  R6 = Resistor [tolerance=±1% resistance=47k package="0402 [SMD]"]
  Step = 3.5mm Switch Jack [part_number=PJ301M-12]
  Reset = 3.5mm Switch Jack [part_number=PJ301M-12]
  S2 = SWITCH-MOMENTARY-2 [package=tactile-pth]
  S1 = SWITCH-MOMENTARY-2 [package=tactile-pth]
  OI = 3.5mm Switch Jack [part_number=PJ301M-12]
  OI2 = 3.5mm Switch Jack [part_number=PJ301M-12]
  IO1 = 3.5mm Switch Jack [part_number=PJ301M-12]
  IO12 = 3.5mm Switch Jack [part_number=PJ301M-12]
  IO10 = 3.5mm Switch Jack [part_number=PJ301M-12]
  IO2 = 3.5mm Switch Jack [part_number=PJ301M-12]
  IO3 = 3.5mm Switch Jack [part_number=PJ301M-12]
  IO11 = 3.5mm Switch Jack [part_number=PJ301M-12]
  IO9 = 3.5mm Switch Jack [part_number=PJ301M-12]
  IO4 = 3.5mm Switch Jack [part_number=PJ301M-12]

nets:
  GND: J8.pin1, C2.+, C1.-, C3.0, C4.0, C5.1, C6.1, C7.0, J9.pin2, J9.pin3, J9.pin4, J9.pin7, J9.pin8, J9.pin9, IC2.5, IC3.5, IC1.8, IC1.13, Q2.2, Q1.2, R4.Pin_1, Q4.2, Q3.2, R6.Pin_1, Step.Pin_1, Reset.Pin_1, OI.Pin_1, OI2.Pin_1, IO1.Pin_1, IO12.Pin_1, IO10.Pin_1, IO2.Pin_1, IO3.Pin_1, IO11.Pin_1, IO9.Pin_1, IO4.Pin_1
  -12V: C2.-, D1.A, C3.1, IC2.4, IC3.4
  12V: C1.+, D2.C, C4.1, C7.1, R15.Pin_0, R14.Pin_0, IC2.12, IC2.13, IC3.12, IC3.13, IC1.16, R2.Pin_0, R3.Pin_0, R5.Pin_0, R7.Pin_0
  Tre: SW1.L1, IC2.8, IC3.8, IC1.7
  N1: SW1.COM, D6.A
  Uno: SW1.L2, IC2.16, IC3.16, IC1.2
  N2: D1.C, J9.pin5, J9.pin6
  N3: D2.A, J9.pin1, J9.pin10
  N4: D8.A, C5.0, S1.2
  CLK: D8.C, IC1.14, D3.C, R4.Pin_0
  N5: D7.A, C6.0, S2.2
  RES: D7.C, D6.C, D5.C, IC1.15, D4.C, R6.Pin_0
  N6: D5.A, IC1.10
  N7: R11.Pin_0, IO2.Pin_3
  IO2: R11.Pin_1, IC2.14
  N8: R15.Pin_1, S2.1
  N9: R14.Pin_1, S1.1
  N10: R18.Pin_0, IO10.Pin_3
  IO2.: R18.Pin_1, IC3.14
  N11: R19.Pin_0, IO12.Pin_3
  IO1.: R19.Pin_1, IC3.3
  Zero: IC2.1, IC3.1, IC1.3
  OI: IC2.2, IC2.7, IC2.10, IC2.15, R9.Pin_1
  IO1: IC2.3, R10.Pin_1
  IO4: IC2.6, R13.Pin_1
  Dos: IC2.9, IC3.9, IC1.4
  IO3: IC2.11, R12.Pin_1, R12_2.Pin_1
  N12: R9.Pin_0, OI.Pin_3
  N13: R20.Pin_0, OI2.Pin_3
  OI.: R20.Pin_1, IC3.2, IC3.7, IC3.10, IC3.15
  IO4.: IC3.6, R16.Pin_1
  IO3.: IC3.11, R17.Pin_1
  N14: R10.Pin_0, IO1.Pin_3
  N15: R12.Pin_0, R12_2.Pin_0, IO3.Pin_3
  N16: R13.Pin_0, IO4.Pin_3
  N17: R16.Pin_0, IO9.Pin_3
  N18: R17.Pin_0, IO11.Pin_3
  N19: R1.Pin_0, Step.Pin_3
  N20: R1.Pin_1, Q2.0
  N21: Q2.1, Q1.0, R2.Pin_1
  N22: Q1.1, R3.Pin_1, D3.A
  N23: Q4.0, R7.Pin_1, Q3.1
  N24: Q4.1, R5.Pin_1, D4.A
  N25: Q3.0, R8.Pin_1
  N26: R8.Pin_0, Reset.Pin_3

custom parts:
  3.5mm Switch Jack: Thonkiconn 3.5mm switching Jack
